// Logisim project chall.circ as structural Verilog: 1 circuit, main circuit main
module main (
  input  _15,
  input  _12,
  input  _8,
  input  _10,
  input  _13,
  input  _14,
  input  _11,
  input  _9,
  input  _7,
  input  _2,
  input  _6,
  input  _1,
  input  _0,
  input  _3,
  input  _4,
  input  _5
);

  wire and_1_out, not_1_out, not_2_out, not_3_out, not_4_out, not_5_out, not_6_out, not_7_out, not_8_out,
       xor_1_out, xor_2_out, xor_3_out, xor_4_out, xor_5_out, xor_6_out, xor_7_out, xor_8_out, xor_9_out,
       xor_10_out, xor_11_out, xor_12_out, xor_13_out, xor_14_out, xor_15_out, xor_16_out;

  xor xor_1 (xor_1_out, _15, _8);
  xor xor_2 (xor_2_out, _12, _13);
  xor xor_3 (xor_3_out, _8, _12);
  xor xor_4 (xor_4_out, _10, _0);
  xor xor_5 (xor_5_out, _13, _9);
  xor xor_6 (xor_6_out, _14, _11);
  xor xor_7 (xor_7_out, _11, _10);
  xor xor_8 (xor_8_out, _9, _14);
  xor xor_9 (xor_9_out, _7, _15);
  xor xor_10 (xor_10_out, _2, _3);
  xor xor_11 (xor_11_out, _6, _1);
  xor xor_12 (xor_12_out, _1, _2);
  xor xor_13 (xor_13_out, _0, _4);
  xor xor_14 (xor_14_out, _3, _5);
  xor xor_15 (xor_15_out, _4, _6);
  xor xor_16 (xor_16_out, _5, _7);
  not not_1 (not_1_out, xor_1_out);
  not not_2 (not_2_out, xor_2_out);
  not not_3 (not_3_out, xor_4_out);
  not not_4 (not_4_out, xor_5_out);
  not not_5 (not_5_out, xor_6_out);
  not not_6 (not_6_out, xor_8_out);
  not not_7 (not_7_out, xor_13_out);
  not not_8 (not_8_out, xor_15_out);
  and and_1 (and_1_out, not_1_out, not_2_out, xor_3_out, not_3_out, not_4_out, not_5_out, xor_7_out, not_6_out, xor_9_out, xor_10_out, xor_11_out, xor_12_out, not_7_out, xor_14_out, not_8_out, xor_16_out);
  LED led_1 (.in(and_1_out));
endmodule
